# Fritzing sketch raif_AD9833 (saved by Fritzing 0.9.3b)

parts:
  LCD1 = LCD screen
  Часть1 = Arduino Uno (Rev3)
  U1 = AD9833 Module
  R1 = Resistor [tolerance=±5% resistance=100 package=THT]
  KEYPAD1 = Membrane Matrix Keypad
  microSD_Transflash1 = SparkFun - microSD Transflash
  R2 = Resistor [tolerance=±5% resistance=4.7k package=THT]
  R3 = Resistor [tolerance=±5% resistance=4.7k package=THT]
  R4 = Resistor [tolerance=±5% resistance=4.7k package=THT]
  R5 = Resistor [tolerance=±5% resistance=10k package=THT]
  R6 = Resistor [tolerance=±5% resistance=10k package=THT]
  R7 = Resistor [tolerance=±5% resistance=10k package=THT]
  SPKR1 = Loudspeaker

nets:
  GND: LCD1.VSS, LCD1.RS, LCD1.LED-, Часть1.GND, U1.DGND, U1.AGND, R1.Pin_0, microSD_Transflash1.GND, R5.Pin_1, R6.Pin_1, R7.Pin_1, SPKR1.pin2
  VDD: LCD1.VDD, LCD1.LED+, Часть1.5V, U1.VCC
  N1: LCD1.V0, R1.Pin_1
  N2: LCD1.R/W, Часть1.D6_PWM
  N3: LCD1.E, Часть1.D7
  N4: LCD1.DB4, Часть1.D5_PWM
  N5: LCD1.DB5, Часть1.D4
  N6: LCD1.DB6, Часть1.D3_PWM
  N7: LCD1.DB7, Часть1.D2
  N8: Часть1.A0, KEYPAD1.1
  N9: Часть1.A1, KEYPAD1.2
  N10: Часть1.A2, KEYPAD1.3
  N11: Часть1.A3, KEYPAD1.4
  N12: Часть1.A4/SDA, KEYPAD1.5
  N13: Часть1.A5/SCL, KEYPAD1.6
  N14: Часть1.D8, KEYPAD1.7
  N15: Часть1.D9_PWM, microSD_Transflash1.CS
  N16: Часть1.D10_PWM/SS, U1.FSYNC
  N17: Часть1.D11_PWM/MOSI, U1.SDATA, R3.Pin_1
  N18: Часть1.D12/MISO, R4.Pin_1
  N19: Часть1.D13/SCK, U1.SCLK, R2.Pin_1
  3V3: Часть1.3V3, microSD_Transflash1.VCC
  N20: U1.OUT, SPKR1.pin1
  N21: microSD_Transflash1.DO, R4.Pin_0, R5.Pin_0
  N22: microSD_Transflash1.SCK, R2.Pin_0, R6.Pin_0
  N23: microSD_Transflash1.DI, R3.Pin_0, R7.Pin_0

custom parts:
  AD9833 Module: programmable waveform generator
  Membrane Matrix Keypad: Membrane Matrix 3x4 Keypad
